# Fritzing sketch circuit_design (saved by Fritzing 0.9.6b)
perfboards: 4

parts:
  R1 = Resistor [tolerance=±5% resistance=10k power=0.25 package=THT]
  D1_(IR_Emitter_Yellow) = LTE-302 (Inverted) [package=lte-302]
  Q1_(IR_Detector_Red) = LTR-301 (Inverted) [package=ltr-301]
  R3 = Resistor [tolerance=±5% resistance=47 power=0.25 package=THT]
  9v_Power_plug_1 = Power plug
  Step_Down_to_5v = RioRand LM2596
  U1 = XD-RF-5V [package=THT]
  J1 = Screw terminal - 2 pins [package=THT]
  J2 = Screw terminal - 2 pins [package=THT]
  R4 = Resistor [tolerance=±5% resistance=10k power=0.25 package=THT]
  D2_(IR_Emitter_Yellow) = LTE-302 (Inverted) [package=lte-302]
  J3 = Screw terminal - 2 pins [package=THT]
  J4 = Screw terminal - 2 pins [package=THT]
  Q2_(IR_Detector_Red) = LTR-301 (Inverted) [package=ltr-301]
  R5 = Resistor [tolerance=±5% resistance=47 power=0.25 package=THT]
  J6 = female pin header, 4 pins [form="♀ (female)"]
  J7 = female pin header, 4 pins [form="♀ (female)"]
  S1_(Garage_Remote) = Pushbutton [package="[THT]"]
  M1 = DOIT Esp32 DevKit v1 (30 pins long, 11 pins width) [part_number=ESP32S-PIN30]
  Power_LED = LED - 5mm [color="Green (555nm)" current=0.030 package="5 mm [THT]"]
  S2 = Pushbutton [package="[THT]"]
  Part2 = I2C level shifter bidirectional
  WiFi_LED = LED - 5mm [color="Blue (470nm)" current=0.030 package="5 mm [THT]"]
  Signal_LED = LED - 5mm [color="Green (555nm)" current=0.030 package="5 mm [THT]"]
  Sensor_1 = LED - 5mm [color="Yellow (585nm)" current=0.030 package="5 mm [THT]"]
  Sensor_2 = LED - 5mm [color="Yellow (585nm)" current=0.030 package="5 mm [THT]"]
  R6 = Resistor [tolerance=±5% resistance=10k power=0.25 package=THT]
  R7 = Resistor [tolerance=±5% resistance=380 power=0.25 package=THT]
  R8 = Resistor [tolerance=±5% resistance=380 power=0.25 package=THT]
  R9 = Resistor [tolerance=±5% resistance=4.7k power=0.25 package=THT]
  R10 = Resistor [tolerance=±5% resistance=2.2k power=0.25 package=THT]
  R11 = Resistor [tolerance=±5% resistance=2.2k power=0.25 package=THT]
  J9 = female pin header, 4 pins [form="♀ (female)"]
  J11 = female pin header, 4 pins [form="♀ (female)"]
  J10 = female pin header, 4 pins [form="♀ (female)"]
  J12 = female pin header, 4 pins [form="♀ (female)"]
  J8 = female pin header, 3 pins [form="♀ (female)"]
  R12 = Resistor [tolerance=±5% power=0.25 resistance=220 package=THT]
  Q1 = NPN-Transistor [part_number=BC548 package="TO92 [THT]"]
  J13 = female pin header, 2 pins [form="♀ (female)"]
  D1 = Rectifier Diode [part_number=1N4001 package="300 mil [THT]"]
  5v_Relay = OMRON PCB Power Relay – G5LE [part_number=HRS1H-S-DC5V package=THT]

nets:
  3.3V: R1.Pin_0, J2.pin2, R4.Pin_0, J4.pin2, J6.pin2, M1.3V3, S2.Pin_3, S2.Pin_4, Part2.LV, J11.pin4, J12.pin1
  N1: R1.Pin_1, Q1_(IR_Detector_Red).C, J2.pin1, J7.pin4, M1.D34
  GND: D1_(IR_Emitter_Yellow).C, Q1_(IR_Detector_Red).E, 9v_Power_plug_1.GND, Step_Down_to_5v.Pin_2, Step_Down_to_5v.Pin_4, U1.GND, J1.pin2, D2_(IR_Emitter_Yellow).C, J3.pin2, Q2_(IR_Detector_Red).E, J6.pin1, M1.GND, Part2.GND, J9.pin4, J10.pin1, J8.pin1, Q1.E
  N2: D1_(IR_Emitter_Yellow).A, R3.Pin_1
  N3: R3.Pin_0, J1.pin1, J6.pin4, M1.D32
  9V: 9v_Power_plug_1.VCC, Step_Down_to_5v.Pin_1
  5V: Step_Down_to_5v.Pin_3, U1.VCC, M1.VIN, Part2.HV, J8.pin3, D1.cathode, 5v_Relay.COIL1
  N4: U1.DATA, Part2.HV1
  N5: R4.Pin_1, J4.pin1, Q2_(IR_Detector_Red).C, J7.pin3, M1.D35
  N6: D2_(IR_Emitter_Yellow).A, R5.Pin_1
  N7: J3.pin1, R5.Pin_0, J6.pin3, M1.D33
  N8: S1_(Garage_Remote).Pin_1, S1_(Garage_Remote).Pin_2, J13.pin2, 5v_Relay.B
  N9: S1_(Garage_Remote).Pin_3, S1_(Garage_Remote).Pin_4, J13.pin1, 5v_Relay.C
  N10: M1.D15, S2.Pin_1, S2.Pin_2, R6.Pin_0, J9.pin3, J10.pin2
  N11: M1.D4, Signal_LED.anode, J9.pin2, J10.pin3
  N12: M1.D5, Sensor_1.anode, J9.pin1, J10.pin4
  N13: M1.D18, Sensor_2.anode, J11.pin1, J12.pin4
  N14: M1.D19, WiFi_LED.anode, J11.pin2, J12.pin3
  N15: M1.D21, Power_LED.anode, J11.pin3, J12.pin2
  N16: M1.D25, Part2.LV2
  N17: M1.D27, Part2.LV1
  N18: Power_LED.cathode, R8.Pin_0
  N19: Part2.HV2, J8.pin2, R12.Pin_1
  N20: WiFi_LED.cathode, R9.Pin_0
  N21: Signal_LED.cathode, R7.Pin_0
  N22: Sensor_1.cathode, R10.Pin_0
  N23: Sensor_2.cathode, R11.Pin_0
  N24: R6.Pin_1, R7.Pin_1, R8.Pin_1, R9.Pin_1, R10.Pin_1, R11.Pin_1
  N25: R12.Pin_0, Q1.B
  N26: Q1.C, D1.anode, 5v_Relay.COIL2

custom parts:
  LTE-302 (Inverted): Through-hole side-firing 940nm IR LED
  LTR-301 (Inverted): Through-hole side-receiving IR phototransistor
  XD-RF-5V: This is 433Mhz RF transmitter with receiver kit for Arduino ARM MCU wireless Application environment: Remote control switch, receiver module, motorcycles, automobile anti-theft products, home security products, electric doors, shutter doors, windows, remote control socket, remote control LED, remote audio remote control electric doors, garage door remote control, remote control retractable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
  DOIT Esp32 DevKit v1 (30 pins long, 11 pins width): The DOIT Esp32 DevKit v1 is one of the development board created by DOIT to evaluate the ESP-WROOM-32 module. It is based on the ESP32 microcontroller that boasts Wifi, Bluetooth, Ethernet and Low Power support all in a single chip. (vanepp) made breadboard work, adjusted pin numbering and labels and reduced size of schematic and cleaned up pcb. This chip is 30pins long (2 x15) and 11 pins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
  OMRON PCB Power Relay – G5LE: A Cubic, Single-pole 10-A Power Relay - ROHS compliant - Sub-miniature ‘sugar cube’ relay with universal terminal footprint - Conforms to EN 61810-1, UL508, CSA22.2 - Tracking resistance: CTI>250 (-VD type) - UL class-F coil insulation model available (UL class-B coil insulation for standard model) - High switching power: 10 A - Two types of seal available; flux protection and fully sealed -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
